# Fritzing sketch Untitled Sketch 2 (saved by Fritzing 0.9.3b)
circuit board: 7.09165cm x 5.53444cm
breadboards: 1

parts:
  Part1 = Arduino Uno (Rev3) - ICSP
  LED1 = LED - 5mm [color="Green (555nm)" package="5 mm [THT]"]
  R1 = Resistor [tolerance=±5% resistance=220 package=THT]
  S1 = Pushbutton [package="[THT]"]
  S2 = Pushbutton [package="[THT]"]
  R2 = Resistor [tolerance=±5% resistance=1k package=THT]
  R3 = Resistor [tolerance=±5% resistance=220 package=THT]
  R4 = Resistor [tolerance=±5% resistance=220 package=THT]
  J1 = Piezo Speaker
  S3 = Pushbutton [package="[THT]"]

nets:
  N1: Part1.ICSP_MISO, Part1.D12/MISO, S1.Pin_1, S1.Pin_2, R2.Pin_1
  N2: Part1.5V, R2.Pin_0, R3.Pin_0, R4.Pin_0
  N3: Part1.ICSP_SCK, Part1.D13/SCK, LED1.cathode
  N4: Part1.ICSP_MOSI, Part1.D11_PWM/MOSI, S2.Pin_1, S2.Pin_2, R3.Pin_1
  N5: Part1.GND, R1.Pin_0, S1.Pin_3, S1.Pin_4, S2.Pin_3, S2.Pin_4, J1.pin1, S3.Pin_1, S3.Pin_2
  N6: Part1.D9_PWM, J1.pin2
  N7: Part1.D10_PWM/SS, R4.Pin_1, S3.Pin_3, S3.Pin_4
  N8: LED1.anode, R1.Pin_1
